// Logisim project Control.circ as structural Verilog: 2 circuits, main circuit Decoder
module Decoder (
  input  A,
  input  B
);

  wire and_1_out, and_2_out, and_3_out, and_4_out;

  LED D0 (.in(and_1_out));
  and and_1 (and_1_out, ~A, ~B);  // AND_Gate
  LED D1 (.in(and_2_out));
  and and_2 (and_2_out, ~A, B);  // AND_Gate
  LED D2 (.in(and_3_out));
  and and_3 (and_3_out, A, ~B);  // AND_Gate
  and and_4 (and_4_out, A, B);
  LED D3 (.in(and_4_out));
endmodule

module Multiplexer (
  input  A0,
  input  S0,
  input  S1,
  input  A1,
  input  A2,
  input  A3
);

  wire and_1_out, and_2_out, and_3_out, and_4_out, or_1_out;

  and and_1 (and_1_out, A0, ~S0, ~S1);  // AND_Gate
  and and_2 (and_2_out, A1, ~S0, S1);  // AND_Gate
  and and_3 (and_3_out, A2, S0, ~S1);  // AND_Gate
  and and_4 (and_4_out, A3, S0, S1);
  or or_1 (or_1_out, and_1_out, and_2_out, and_3_out, and_4_out);
  LED Output (.in(or_1_out));
endmodule
